# Fritzing sketch EMFTransistor (saved by Fritzing 0.8.7b)
circuit board: 3.79588cm x 2.77425cm
breadboards: 1

parts:
  ANT1 = Antenna
  Q8 = PNP-Transistor [package="SOT-23 [SMD]"]
  Q9 = NPN-Transistor [package="SOT-23 [SMD]"]
  Q11 = NPN-Transistor [package="SOT-23 [SMD]"]
  Q12 = NPN-Transistor [package="SOT-23 [SMD]"]
  BAT2 = Battery Holders [package=battcon_20mm_4legs]
  part = Audio Jack (TRRS) 3.5mm [part_number="LUMBERG JEITA RC-5325A" package="RC-5325A [SMD]"]
  Q10 = NPN-Transistor [package="SOT-23 [SMD]"]

nets:
  N1: ANT1.antenna_lead, Q8.0
  N2: Q8.2, Q9.1, Q11.1, Q12.1, BAT2.+, Q10.1
  N3: Q8.1, Q9.0
  N4: Q9.2, Q10.0
  N5: Q11.2, Q12.0
  N6: Q11.0, Q10.2
  N7: Q12.2, part.TIP
  N8: BAT2.-, part.SLEEVE
