# Fritzing sketch tinyEMF (saved by Fritzing 0.8.7b)
breadboards: 1

parts:
  U1 = attiny85 [package=dip]  # not connected
  U3 = LIPO-110mAh [package=lipo-110]
  U4 = 3.5mm Audio Jack [package=audio-jack-3.5mm-smd]
  JP1 = Header 2 [package=jst-2-pth]
  Q2 = Basic FET N-Channel [package="DPak [SMD]"]
  L1 = Inductor [package="400 mil [THT]"]
  R1 = Resistor [tolerance=±5% resistance=3.3M package=THT]
  U5 = Vibration Motor- ROB-08449 [package=vibe-motor-10mm]
  LED1 = LED - 3mm [color="White (4500K)" package="3 mm [THT]"]
  R2 = Resistor [tolerance=±5% resistance=100 package=THT]

nets:
  N1: U3.+, JP1.2, U5.-
  N2: U3.-, U4.SLEEVE, JP1.1, R1.Pin_0, LED1.cathode
  N3: U4.RIGHT, U4.LEFT
  N4: Q2.Gate, R2.Pin_1
  N5: Q2.drain, U5.+
  N6: L1.pin_1, R1.Pin_1
